// Logisim project processeur_ARO2.circ as structural Verilog: 23 circuits, main circuit main
module main (
);

  wire clk, CPU_ARO_memory_high_byte_o, CPU_ARO_memory_ldr_data, CPU_ARO_memory_low_byte_o,
       CPU_ARO_memory_str_data_o, high_write_en_s, low_write_en_s, RESET_out, sysclk;
  wire [0:0] CPU_ARO_instr_addr_o;
  wire [7:0] rd_data_high_s, rd_data_low_s, wr_data_high_s, wr_data_low_s;
  wire [14:0] CPU_ARO_instr_addr_o_2, memory_addr_s;
  wire [15:0] CPU_ARO_memory_wr_data_o, InstrMemory_data, rd_data_s;

  Button RESET (.out(RESET_out));
  Clock #(.highDuration(4), .lowDuration(4)) u_clk (.out(clk));
  Clock u_sysclk (.out(sysclk));
  // Probe on CPU_ARO_instr_addr_o_2
  ROM #(.addrWidth(15), .dataWidth(16)) InstrMemory (.addr(CPU_ARO_instr_addr_o_2), .data(InstrMemory_data));
  // Probe on InstrMemory_data
  processeur_ARO2 CPU_ARO (
    .instr_data_i(InstrMemory_data), .memory_rd_data_i(rd_data_s), .rst_i(RESET_out), .clk_i(clk),
    .instr_addr_o({CPU_ARO_instr_addr_o_2, CPU_ARO_instr_addr_o[0]}), .memory_addr_o(memory_addr_s),
    .memory_wr_data_o(CPU_ARO_memory_wr_data_o), .memory_str_data_o(CPU_ARO_memory_str_data_o),
    .memory_ldr_data(CPU_ARO_memory_ldr_data), .memory_high_byte_o(CPU_ARO_memory_high_byte_o),
    .memory_low_byte_o(CPU_ARO_memory_low_byte_o));
  // Probe on CPU_ARO_instr_addr_o_2
  RAM #(.addrWidth(15), .databus("bibus")) DataMemoryHigh (
    .addr(memory_addr_s), .we(high_write_en_s), .oe(1'b1), .clk(sysclk), .din(wr_data_high_s),
    .dout(rd_data_high_s));
  RAM #(.addrWidth(15), .databus("bibus")) DataMemoryLow (
    .addr(memory_addr_s), .we(low_write_en_s), .oe(1'b1), .clk(sysclk), .din(wr_data_low_s),
    .dout(rd_data_low_s));
  memory_controller Memoire_controller (
    .wr_data_i(CPU_ARO_memory_wr_data_o), .str_data_i(CPU_ARO_memory_str_data_o),
    .ldr_data_i(CPU_ARO_memory_ldr_data), .high_byte_i(CPU_ARO_memory_high_byte_o),
    .low_byte_i(CPU_ARO_memory_low_byte_o), .rd_data_high_i(rd_data_high_s), .rd_data_low_i(rd_data_low_s),
    .rd_data_o(rd_data_s), .high_data_o(wr_data_high_s), .low_data_o(wr_data_low_s),
    .high_write_en_o(high_write_en_s), .low_write_en_o(low_write_en_s));

  // Notes on the sheet:
  //   Attention, votre version de Logisim
  //   ne contient pas de tracker. Si vous
  //   enregistrez votre projet, toutes les
  //   informations du tracker seront
  //   définitivement effacées.
  //   contents of InstrMemory (hex, n*v repeats v):
  //   2106 2204 2303 2403 5508
endmodule

module memory_controller (
  input  [15:0] wr_data_i,
  input  str_data_i,
  input  ldr_data_i,
  input  high_byte_i,
  input  low_byte_i,
  input  [7:0] rd_data_high_i,
  input  [7:0] rd_data_low_i,
  output [15:0] rd_data_o,
  output [7:0] high_data_o,
  output [7:0] low_data_o,
  output high_write_en_o,
  output low_write_en_o
);

  wire ADN4_out, AND2_out, AND3_out, not_1_out;
  wire [7:0] multiplexer_2_out, multiplexer_3_out;

  and AND0 (low_write_en_o, low_byte_i, str_data_i);
  and AND1 (high_write_en_o, high_byte_i, str_data_i);
  and AND2 (AND2_out, low_byte_i, high_byte_i);
  and AND3 (AND3_out, high_byte_i, ~low_byte_i);  // AND_Gate
  not not_1 (not_1_out, ADN4_out);
  and ADN4 (ADN4_out, high_byte_i, low_byte_i);
  Multiplexer #(.width(8), .enable("false")) multiplexer_1 (
    .in0(wr_data_i[7:0]), .in1(wr_data_i[15:8]), .out(high_data_o), .sel(AND2_out));
  Multiplexer #(.width(8), .enable("false")) multiplexer_2 (
    .in0(rd_data_low_i), .in1(rd_data_high_i), .out(multiplexer_2_out), .sel(AND3_out));
  Multiplexer #(.width(8), .enable("false")) multiplexer_3 (
    .in0(rd_data_high_i), .in1({8{1'b0}}), .out(multiplexer_3_out), .sel(not_1_out));
  assign rd_data_o = ldr_data_i ? {multiplexer_3_out, multiplexer_2_out} : 16'bz;  // Controlled_Buffer controlled_buffer_1

  assign low_data_o = wr_data_i[7:0];

  // Other names for the same wires on the sheet: wr_data_high_o[7:0] = high_data_o;
  //   wr_data_low_o[7:0] = wr_data_i[7:0]

  // Notes on the sheet:
  //   Attention, votre version de Logisim
  //   ne contient pas de tracker. Si vous
  //   enregistrez votre projet, toutes les
  //   informations du tracker seront
  //   définitivement effacées.
  //   Write interface
  //   Read interface
endmodule

module processeur_ARO2 (
  input  [15:0] instr_data_i,
  input  [15:0] memory_rd_data_i,
  input  rst_i,
  input  clk_i,
  output [15:0] instr_addr_o,
  output [14:0] memory_addr_o,
  output [15:0] memory_wr_data_o,
  output memory_str_data_o,
  output memory_ldr_data,
  output memory_high_byte_o,
  output memory_low_byte_o
);

  wire bloc_decode_decode_en_o, bloc_fetch_branch_o, execute_en_s, fetch_en_s, link_en_s, memory_acc_en_s,
       reg_bank_en_s;
  wire [1:0] reg_bank_control_bus;
  wire [2:0] adr_reg_d, adr_reg_m, adr_reg_mem, adr_reg_n, bloc_decode_imm3_o;
  wire [3:0] cpsr_s;
  wire [4:0] bloc_decode_imm5_o, mem_control_bus;
  wire [6:0] fetch_control_bus;
  wire [7:0] bloc_decode_imm8_o, bloc_decode_offset8_o;
  wire [10:0] bloc_decode_offset11_o;
  wire [14:0] execute_control_bus;
  wire [15:0] Bloc_execute_data_out_o, bloc_fetch_instr_data_o, bloc_fetch_lr_addr_o, bloc_fetch_pc_fut_o,
       bloc_memory_access_mem_adr_byte_o, jump_adr_s, PC_pres_s, reg_m_read_data_s, reg_mem_read_data_s,
       reg_n_read_data_s;

  // Probe on instr_data_i
  fetch bloc_fetch (
    .fetch_en_i(fetch_en_s), .instr_data_i(instr_data_i), .PC_pres_i(PC_pres_s), .branch_addr_i(jump_adr_s),
    .fetch_control_bus_i(fetch_control_bus), .cpsr_i(cpsr_s), .clk_i(clk_i), .rst_i(rst_i),
    .instr_addr_o(instr_addr_o), .instr_data_o(bloc_fetch_instr_data_o), .PC_fut_o(bloc_fetch_pc_fut_o),
    .LR_addr_o(bloc_fetch_lr_addr_o), .branch_o(bloc_fetch_branch_o));
  // Probe on instr_addr_o
  // Probe on jump_adr_s
  decode bloc_decode (
    .instr_data_i(bloc_fetch_instr_data_o), .rst_i(rst_i), .clk_i(clk_i), .adr_reg_d_o(adr_reg_d),
    .adr_reg_n_o(adr_reg_n), .adr_reg_m_o(adr_reg_m), .adr_reg_mem_o(adr_reg_mem),
    .imm3_o(bloc_decode_imm3_o), .imm5_o(bloc_decode_imm5_o), .offset11_o(bloc_decode_offset11_o),
    .offset8_o(bloc_decode_offset8_o), .imm8_o(bloc_decode_imm8_o),
    .reg_bank_control_bus_o(reg_bank_control_bus), .execute_control_bus_o(execute_control_bus),
    .mem_control_bus_o(mem_control_bus), .fetch_control_bus_o(fetch_control_bus), .link_en_o(link_en_s),
    .fetch_en_o(fetch_en_s), .decode_en_o(bloc_decode_decode_en_o), .reg_bank_en_o(reg_bank_en_s),
    .execute_en_o(execute_en_s), .memory_access_en_o(memory_acc_en_s));
  // Probe on bloc_decode_decode_en_o
  bank_registers bloc_bank_register (
    .clk_i(clk_i), .rst_i(rst_i), .register_d_sel_i(adr_reg_d), .register_d_data_i(jump_adr_s),
    .register_n_sel_i(adr_reg_n), .register_m_sel_i(adr_reg_m), .register_mem_sel_i(adr_reg_mem),
    .reg_bank_control_bus_i(reg_bank_control_bus), .PC_fut_i(bloc_fetch_pc_fut_o),
    .LR_addr_i(bloc_fetch_lr_addr_o), .branch_i(bloc_fetch_branch_o), .link_en_i(link_en_s),
    .reg_bank_en_i(reg_bank_en_s), .register_n_read_data_o(reg_n_read_data_s),
    .register_m_read_data_o(reg_m_read_data_s), .register_mem_read_data_o(reg_mem_read_data_s),
    .PC_pres_o(PC_pres_s));
  execute Bloc_execute (
    .reg_data_n_i(reg_n_read_data_s), .reg_data_m_i(reg_m_read_data_s), .imm3(bloc_decode_imm3_o),
    .imm5(bloc_decode_imm5_o), .offset_incond(bloc_decode_offset11_o), .offset_cond(bloc_decode_offset8_o),
    .imm8(bloc_decode_imm8_o), .execute_control_bus(execute_control_bus), .rst_i(rst_i), .clk_i(clk_i),
    .execute_en_i(execute_en_s), .data_out_o(Bloc_execute_data_out_o), .cpsr_o(cpsr_s));
  memory_access bloc_memory_access (
    .mem_data_i(memory_rd_data_i), .reg_data_i(reg_mem_read_data_s), .data_i(Bloc_execute_data_out_o),
    .memory_control_bus_i(mem_control_bus), .rst_i(rst_i), .clk_i(clk_i), .mem_access_en_i(memory_acc_en_s),
    .mem_data_adr_o(memory_addr_o), .mem_adr_byte_o(bloc_memory_access_mem_adr_byte_o),
    .mem_data_out_o(memory_wr_data_o), .mem_out_o(jump_adr_s), .str_data_o(memory_str_data_o),
    .ldr_data_o(memory_ldr_data), .high_byte_o(memory_high_byte_o), .low_byte_o(memory_low_byte_o));
  // Probe on bloc_memory_access_mem_adr_byte_o

  // Other names for the same wires on the sheet: clk_s = clk_i; instr_addr_s[15:0] = instr_addr_o;
  //   instr_data_s[15:0] = instr_data_i; memory_addr_s[14:0] = memory_addr_o; memory_high_byte_s = memory_high_byte_o;
  //   memory_ldr_data_s = memory_ldr_data; memory_low_byte_s = memory_low_byte_o;
  //   memory_rd_data_s[15:0] = memory_rd_data_i; memory_str_data_s = memory_str_data_o;
  //   memory_wr_data_s[15:0] = memory_wr_data_o; rst_s = rst_i

  // Notes on the sheet:
  //   Attention, votre version de Logisim
  //   ne contient pas de tracker. Si vous
  //   enregistrez votre projet, toutes les
  //   informations du tracker seront
  //   définitivement effacées.
  //   Intruction memory inputs
  //   Memory interface inputs
  //   Standard inputs
  //   Processeur simplifié pour le cours ARO2
  //   Instruction memory outputs
  //   Memory interface outputs
endmodule

module fetch (
  input  fetch_en_i,
  input  [15:0] instr_data_i,
  input  [15:0] PC_pres_i,
  input  [15:0] branch_addr_i,
  input  [6:0] fetch_control_bus_i,
  input  [3:0] cpsr_i,
  input  clk_i,
  input  rst_i,
  output [15:0] instr_addr_o,
  output [15:0] instr_data_o,
  output [15:0] PC_fut_o,
  output [15:0] LR_addr_o,
  output branch_o
);

  wire cond_test_s;
  wire [15:0] multiplexer_1_out;

  Multiplexer #(.width(16), .enable("false")) multiplexer_1 (
    .in0(LR_addr_o), .in1(branch_addr_i), .out(multiplexer_1_out), .sel(branch_o));
  Adder #(.width(16)) adder_1 (.a(PC_pres_i), .b(16'h2), .out(LR_addr_o));  // open: cin, cout
  and AND0 (branch_o, fetch_control_bus_i[0], cond_test_s);
  Multiplexer #(.width(16), .enable("false")) multiplexer_2 (
    .in0(PC_pres_i), .in1(multiplexer_1_out), .out(PC_fut_o), .sel(fetch_en_i));
  condition_tester bloc_condition_tester (
    .cond_en_i(fetch_control_bus_i[1]), .cond_i(fetch_control_bus_i[5:2]), .Z_i(cpsr_i[0]), .C_i(cpsr_i[1]),
    .N_i(cpsr_i[2]), .V_i(cpsr_i[3]), .cond_test_o(cond_test_s));

  assign instr_addr_o = PC_pres_i;
  assign instr_data_o = instr_data_i;

  // Other names for the same wires on the sheet: branch_addr_s[15:0] = branch_addr_i; branch_s = branch_o;
  //   cpsr_s[3:0] = cpsr_i; fetch_control_bus_s[6:0] = fetch_control_bus_i; sel_PC_s = fetch_control_bus_i[0];
  //   cond_en_s = fetch_control_bus_i[1]; cond_s[3:0] = fetch_control_bus_i[5:2]; fetch_en_s = fetch_en_i;
  //   instr_addr_s[15:0] = PC_pres_i; PC_pres_s[15:0] = PC_pres_i; instr_data_s[15:0] = instr_data_i;
  //   PC_fut_s[15:0] = PC_fut_o; PC_pres_incr_s[15:0] = LR_addr_o

  // Notes on the sheet:
  //   Attention, votre version de Logisim
  //   ne contient pas de tracker. Si vous
  //   enregistrez votre projet, toutes les
  //   informations du tracker seront
  //   définitivement effacées.
  //   Entité FETCH
  //   Increment du PC
  //   Control bus splitting
  //   Permet le saut
  //   L'état de PC va directement sur l'adresse d'instruction
endmodule

module condition_tester (
  input  cond_en_i,
  input  [3:0] cond_i,
  input  Z_i,
  input  C_i,
  input  N_i,
  input  V_i,
  output cond_test_o
);

  wire AND0_out, AND1_out, comparator_1_eq, not_1_out, not_2_out, not_3_out, not_4_out, not_5_out, not_6_out,
       not_7_out, not_8_out, OR0_out, OR1_out;
  wire [3:0] multiplexer_1_out;

  and AND0 (AND0_out, C_i, not_1_out);
  not not_1 (not_1_out, Z_i);
  not not_2 (not_2_out, C_i);
  or OR0 (OR0_out, not_2_out, Z_i);
  Comparator #(.width(1), .mode("unsigned")) comparator_1 (.a(N_i), .b(V_i), .eq(comparator_1_eq));  // open: gt, lt
  not not_3 (not_3_out, Z_i);
  not not_4 (not_4_out, comparator_1_eq);
  and AND1 (AND1_out, comparator_1_eq, not_3_out);
  or OR1 (OR1_out, not_4_out, Z_i);
  not not_5 (not_5_out, Z_i);
  not not_6 (not_6_out, C_i);
  not not_7 (not_7_out, N_i);
  not not_8 (not_8_out, V_i);
  Multiplexer #(.width(4), .enable("false")) multiplexer_1 (
    .in0(4'b1110), .in1(cond_i), .out(multiplexer_1_out), .sel(cond_en_i));
  Multiplexer #(.select(4), .enable("false")) multiplexer_2 (
    .in0(Z_i), .in1(not_5_out), .in2(C_i), .in3(not_6_out), .in4(N_i), .in5(not_7_out), .in6(V_i),
    .in7(not_8_out), .in8(AND0_out), .in9(OR0_out), .in10(comparator_1_eq), .in11(not_4_out),
    .in12(AND1_out), .in13(OR1_out), .in14(1'b1), .in15(1'b1), .out(cond_test_o), .sel(multiplexer_1_out));

  // Notes on the sheet:
  //   Attention, votre version de Logisim
  //   ne contient pas de tracker. Si vous
  //   enregistrez votre projet, toutes les
  //   informations du tracker seront
  //   définitivement effacées.
  //   Always (Inconditionnel)
endmodule

module decode (
  input  [15:0] instr_data_i,
  input  rst_i,
  input  clk_i,
  output [2:0] adr_reg_d_o,
  output [2:0] adr_reg_n_o,
  output [2:0] adr_reg_m_o,
  output [2:0] adr_reg_mem_o,
  output [2:0] imm3_o,
  output [4:0] imm5_o,
  output [10:0] offset11_o,
  output [7:0] offset8_o,
  output [7:0] imm8_o,
  output [1:0] reg_bank_control_bus_o,
  output [14:0] execute_control_bus_o,
  output [4:0] mem_control_bus_o,
  output [6:0] fetch_control_bus_o,
  output link_en_o,
  output fetch_en_o,
  output decode_en_o,
  output reg_bank_en_o,
  output execute_en_o,
  output memory_access_en_o
);

  wire [2:0] rd_2_0_s, rd_10_8_s, rm_8_6_s, rn_5_3_s;
  wire [3:0] cond_s;
  wire [5:0] decode_control_bus_s;

  decode_instr_splitter Instr_Splitter_Inst (
    .instr_i(instr_data_i), .rd_2_0_o(rd_2_0_s), .rd_10_8_o(rd_10_8_s), .rn_5_3_o(rn_5_3_s),
    .rm_8_6_o(rm_8_6_s), .offset3_8_6_o(imm3_o), .offset5_10_6_o(imm5_o), .offset8_7_0_o(imm8_o),
    .offset11_10_0_o(offset11_o), .cond_11_8_o(cond_s));
  main_control_unit Control_Unit_Inst (
    .instr_i(instr_data_i), .cond_i(cond_s), .fetch_control_bus_o(fetch_control_bus_o),
    .decode_control_bus_o({decode_control_bus_s[5:4], link_en_o, decode_control_bus_s[2:0]}),
    .reg_bank_control_bus_o(reg_bank_control_bus_o), .execute_control_bus_o(execute_control_bus_o),
    .mem_control_bus_o(mem_control_bus_o), .fetch_en_o(fetch_en_o), .decode_en_o(decode_en_o),
    .reg_bank_en_o(reg_bank_en_o), .execute_en_o(execute_en_o), .memory_access_en_o(memory_access_en_o));
  Multiplexer #(.width(3), .enable("false")) multiplexer_1 (
    .in0(rm_8_6_s), .in1(rn_5_3_s), .out(adr_reg_m_o), .sel(decode_control_bus_s[2]));
  Multiplexer #(.select(2), .width(3), .enable("false")) multiplexer_2 (
    .in0(rn_5_3_s), .in1(adr_reg_d_o), .in2(3'b111), .in3(3'b110), .out(adr_reg_n_o),
    .sel(decode_control_bus_s[1:0]));
  Multiplexer #(.select(3), .width(3), .enable("false")) multiplexer_3 (
    .in0(rd_2_0_s), .in1(rd_2_0_s), .in2(3'b110), .in3(3'b111), .in4(rd_10_8_s), .in5(rd_10_8_s),
    .in6(3'b110), .in7(3'b111), .out(adr_reg_d_o), .sel({decode_control_bus_s[4], decode_control_bus_s[1:0]}));

  assign adr_reg_mem_o = adr_reg_d_o;
  assign offset8_o = imm8_o;

  // Other names for the same wires on the sheet: sel_rn[1:0] = decode_control_bus_s[1:0];
  //   sel_rd = decode_control_bus_s[4]; adr_reg_d_s[2:0] = adr_reg_d_o; adr_reg_m_s[2:0] = adr_reg_m_o;
  //   adr_reg_n_s[2:0] = adr_reg_n_o; sel_rm = decode_control_bus_s[2]; decode_control_bus_s[3] = link_en_o;
  //   link_en_s = link_en_o; offset3_8_6_s[2:0] = imm3_o; offset5_10_6_s[4:0] = imm5_o; offset8_7_0_s[7:0] = imm8_o;
  //   offset11_10_0_s[10:0] = offset11_o

  // Notes on the sheet:
  //   Attention, votre version de Logisim
  //   ne contient pas de tracker. Si vous
  //   enregistrez votre projet, toutes les
  //   informations du tracker seront
  //   définitivement effacées.
  //   Entité DECODE
endmodule

module decode_instr_splitter (
  input  [15:0] instr_i,
  output [2:0] rd_2_0_o,
  output [2:0] rd_10_8_o,
  output [2:0] rn_5_3_o,
  output [2:0] rm_8_6_o,
  output [2:0] offset3_8_6_o,
  output [4:0] offset5_10_6_o,
  output [7:0] offset8_7_0_o,
  output [10:0] offset11_10_0_o,
  output [3:0] cond_11_8_o
);


  assign cond_11_8_o = instr_i[11:8];
  assign offset3_8_6_o = instr_i[8:6];
  assign offset5_10_6_o = instr_i[10:6];
  assign offset8_7_0_o = instr_i[7:0];
  assign offset11_10_0_o = instr_i[10:0];
  assign rd_2_0_o = instr_i[2:0];
  assign rd_10_8_o = instr_i[10:8];
  assign rm_8_6_o = instr_i[8:6];
  assign rn_5_3_o = instr_i[5:3];

  // Notes on the sheet:
  //   Attention, votre version de Logisim
  //   ne contient pas de tracker. Si vous
  //   enregistrez votre projet, toutes les
  //   informations du tracker seront
  //   définitivement effacées.
endmodule

module main_control_unit (
  input  [15:0] instr_i,
  input  [3:0] cond_i,
  output [6:0] fetch_control_bus_o,
  output [5:0] decode_control_bus_o,
  output [1:0] reg_bank_control_bus_o,
  output [14:0] execute_control_bus_o,
  output [4:0] mem_control_bus_o,
  output fetch_en_o,
  output decode_en_o,
  output reg_bank_en_o,
  output execute_en_o,
  output memory_access_en_o
);

  wire add_r_imm_s, add_r_r_imm_s, add_r_r_r_s, and_r_r_s, asr_r_r_imm_s, asr_r_r_s, b_cond_s, b_incond_s,
       bl_lsb_s, bl_msb_s, byte_s, cond_en_s, eor_r_r_s, ldr_data_s, ldrb_r_r_imm_s, ldrb_r_r_r_s,
       ldrh_r_r_imm_s, ldrh_r_r_r_s, link_en_s, lsl_r_r_imm_s, lsl_r_r_s, lsr_r_r_imm_s, lsr_r_r_s,
       mov_r_imm_s, mvn_r_r_s, neg_r_r_s, orr_r_r_s, reg_bank_wr_s, ror_r_r_s, sel_cpsr_s, sel_mem_s,
       sel_operand_1_s, sel_PC_s, sel_rd_s, sel_rm_s, sel_shift_s, str_data_s, strb_r_r_imm_s, strb_r_r_r_s,
       strh_r_r_imm_s, strh_r_r_r_s, sub_r_imm_s, sub_r_r_imm_s, sub_r_r_r_s;
  wire [1:0] sel_operand_2_s, sel_rn_s;
  wire [2:0] sel_mult_2_s, sel_op_alu_s, sel_op_shift_s;

  opcode_supported_unit bloc_opcode_supported_unit (
    .instr_i(instr_i), .lsl_r_r_imm_o(lsl_r_r_imm_s), .lsr_r_r_imm_o(lsr_r_r_imm_s),
    .asr_r_r_imm_o(asr_r_r_imm_s), .add_r_r_r_o(add_r_r_r_s), .add_r_r_imm_o(add_r_r_imm_s),
    .sub_r_r_r_o(sub_r_r_r_s), .sub_r_r_imm_o(sub_r_r_imm_s), .mov_r_imm_o(mov_r_imm_s),
    .add_r_imm_o(add_r_imm_s), .sub_r_imm_o(sub_r_imm_s), .and_r_r_o(and_r_r_s), .eor_r_r_o(eor_r_r_s),
    .lsl_r_r_o(lsl_r_r_s), .lsr_r_r_o(lsr_r_r_s), .asr_r_r_o(asr_r_r_s), .ror_r_r_o(ror_r_r_s),
    .neg_r_r_o(neg_r_r_s), .orr_r_r_o(orr_r_r_s), .mvn_r_r_o(mvn_r_r_s), .strb_r_r_r_o(strb_r_r_r_s),
    .ldrb_r_r_r_o(ldrb_r_r_r_s), .strh_r_r_r_o(strh_r_r_r_s), .ldrh_r_r_r_o(ldrh_r_r_r_s),
    .strb_r_r_imm_o(strb_r_r_imm_s), .ldrb_r_r_imm_o(ldrb_r_r_imm_s), .strh_r_r_imm_o(strh_r_r_imm_s),
    .ldrh_r_r_imm_o(ldrh_r_r_imm_s), .b_cond_o(b_cond_s), .b_incond_o(b_incond_s), .bl_msb_o(bl_msb_s),
    .bl_lsb_o(bl_lsb_s));
  fetch_control_unit fetch (
    .instr_i({1'b0, bl_lsb_s, bl_msb_s, b_incond_s, b_cond_s, ldrh_r_r_imm_s, strh_r_r_imm_s, ldrb_r_r_imm_s, strb_r_r_imm_s, ldrh_r_r_r_s, strh_r_r_r_s, ldrb_r_r_r_s, strb_r_r_r_s, mvn_r_r_s, orr_r_r_s, neg_r_r_s, ror_r_r_s, asr_r_r_s, lsr_r_r_s, lsl_r_r_s, eor_r_r_s, and_r_r_s, sub_r_imm_s, add_r_imm_s, mov_r_imm_s, sub_r_r_imm_s, sub_r_r_r_s, add_r_r_imm_s, add_r_r_r_s, asr_r_r_imm_s, lsr_r_r_imm_s, lsl_r_r_imm_s}),
    .sel_cpsr_o(sel_cpsr_s), .link_en_o(link_en_s), .sel_PC_o(sel_PC_s), .cond_en_o(cond_en_s));
  decode_control_unit decode (
    .instr_i({1'b0, bl_lsb_s, bl_msb_s, b_incond_s, b_cond_s, ldrh_r_r_imm_s, strh_r_r_imm_s, ldrb_r_r_imm_s, strb_r_r_imm_s, ldrh_r_r_r_s, strh_r_r_r_s, ldrb_r_r_r_s, strb_r_r_r_s, mvn_r_r_s, orr_r_r_s, neg_r_r_s, ror_r_r_s, asr_r_r_s, lsr_r_r_s, lsl_r_r_s, eor_r_r_s, and_r_r_s, sub_r_imm_s, add_r_imm_s, mov_r_imm_s, sub_r_r_imm_s, sub_r_r_r_s, add_r_r_imm_s, add_r_r_r_s, asr_r_r_imm_s, lsr_r_r_imm_s, lsl_r_r_imm_s}),
    .sel_rn_o(sel_rn_s), .sel_rm_o(sel_rm_s), .sel_rd_o(sel_rd_s));
  reg_bank_control_unit reg_bank (
    .in_1({1'b0, bl_lsb_s, bl_msb_s, b_incond_s, b_cond_s, ldrh_r_r_imm_s, strh_r_r_imm_s, ldrb_r_r_imm_s, strb_r_r_imm_s, ldrh_r_r_r_s, strh_r_r_r_s, ldrb_r_r_r_s, strb_r_r_r_s, mvn_r_r_s, orr_r_r_s, neg_r_r_s, ror_r_r_s, asr_r_r_s, lsr_r_r_s, lsl_r_r_s, eor_r_r_s, and_r_r_s, sub_r_imm_s, add_r_imm_s, mov_r_imm_s, sub_r_r_imm_s, sub_r_r_r_s, add_r_r_imm_s, add_r_r_r_s, asr_r_r_imm_s, lsr_r_r_imm_s, lsl_r_r_imm_s}),
    .out_2(reg_bank_wr_s));
  execute_control_unit execute (
    .in_1({1'b0, bl_lsb_s, bl_msb_s, b_incond_s, b_cond_s, ldrh_r_r_imm_s, strh_r_r_imm_s, ldrb_r_r_imm_s, strb_r_r_imm_s, ldrh_r_r_r_s, strh_r_r_r_s, ldrb_r_r_r_s, strb_r_r_r_s, mvn_r_r_s, orr_r_r_s, neg_r_r_s, ror_r_r_s, asr_r_r_s, lsr_r_r_s, lsl_r_r_s, eor_r_r_s, and_r_r_s, sub_r_imm_s, add_r_imm_s, mov_r_imm_s, sub_r_r_imm_s, sub_r_r_r_s, add_r_r_imm_s, add_r_r_r_s, asr_r_r_imm_s, lsr_r_r_imm_s, lsl_r_r_imm_s}),
    .out_2(sel_operand_1_s), .out_3(sel_operand_2_s), .out_4(sel_op_shift_s), .out_5(sel_op_alu_s),
    .out_6(sel_mult_2_s), .out_7(sel_shift_s));
  memory_access_control_unit memory_acces (
    .in_1({1'b0, bl_lsb_s, bl_msb_s, b_incond_s, b_cond_s, ldrh_r_r_imm_s, strh_r_r_imm_s, ldrb_r_r_imm_s, strb_r_r_imm_s, ldrh_r_r_r_s, strh_r_r_r_s, ldrb_r_r_r_s, strb_r_r_r_s, mvn_r_r_s, orr_r_r_s, neg_r_r_s, ror_r_r_s, asr_r_r_s, lsr_r_r_s, lsl_r_r_s, eor_r_r_s, and_r_r_s, sub_r_imm_s, add_r_imm_s, mov_r_imm_s, sub_r_r_imm_s, sub_r_r_r_s, add_r_r_imm_s, add_r_r_r_s, asr_r_r_imm_s, lsr_r_r_imm_s, lsl_r_r_imm_s}),
    .out_2(sel_mem_s), .out_3(str_data_s), .out_4(ldr_data_s), .out_5(byte_s));
  bus_constructor bus_constructor_1 (
    .fetch_en_i(1'b0), .decode_en_i(1'b0), .reg_bank_en_i(1'b0), .execute_en_i(1'b0),
    .memory_access_en_i(1'b0), .cond_i(cond_i), .sel_cpsr_i(sel_cpsr_s), .link_en_i(link_en_s),
    .sel_PC_i(sel_PC_s), .cond_en_i(cond_en_s), .sel_rn_i(sel_rn_s), .sel_rm_i(sel_rm_s),
    .sel_rd_i(sel_rd_s), .reg_bank_wr_i(reg_bank_wr_s), .sel_operand_1_i(sel_operand_1_s),
    .sel_operand_2_i(sel_operand_2_s), .sel_op_shift_i(sel_op_shift_s), .sel_op_alu_i(sel_op_alu_s),
    .sel_mult_2_i(sel_mult_2_s), .sel_shift_i(sel_shift_s), .sel_mem_i(sel_mem_s), .str_data_i(str_data_s),
    .ldr_data_i(ldr_data_s), .byte_i(byte_s), .fetch_control_bus_o(fetch_control_bus_o),
    .decode_control_bus_o(decode_control_bus_o), .reg_bank_control_bus_o(reg_bank_control_bus_o),
    .execute_control_bus_o(execute_control_bus_o), .mem_control_bus_o(mem_control_bus_o));

  assign decode_en_o = 1'b1;
  assign execute_en_o = 1'b1;
  assign fetch_en_o = 1'b1;
  assign memory_access_en_o = 1'b1;
  assign reg_bank_en_o = 1'b1;

  // Other names for the same wires on the sheet: cond_s[3:0] = cond_i;
  //   decode_control_bus_s[5:0] = decode_control_bus_o; execute_control_bus_s[14:0] = execute_control_bus_o;
  //   fetch_control_bus_s[6:0] = fetch_control_bus_o; mem_control_bus_s[4:0] = mem_control_bus_o;
  //   reg_bank_control_bus_s[1:0] = reg_bank_control_bus_o

  // Notes on the sheet:
  //   Attention, votre version de Logisim
  //   ne contient pas de tracker. Si vous
  //   enregistrez votre projet, toutes les
  //   informations du tracker seront
  //   définitivement effacées.
endmodule

module opcode_supported_unit (
  input  [15:0] instr_i,
  output lsl_r_r_imm_o,
  output lsr_r_r_imm_o,
  output asr_r_r_imm_o,
  output add_r_r_r_o,
  output add_r_r_imm_o,
  output sub_r_r_r_o,
  output sub_r_r_imm_o,
  output mov_r_imm_o,
  output add_r_imm_o,
  output sub_r_imm_o,
  output and_r_r_o,
  output eor_r_r_o,
  output lsl_r_r_o,
  output lsr_r_r_o,
  output asr_r_r_o,
  output ror_r_r_o,
  output neg_r_r_o,
  output orr_r_r_o,
  output mvn_r_r_o,
  output strb_r_r_r_o,
  output ldrb_r_r_r_o,
  output strh_r_r_r_o,
  output ldrh_r_r_r_o,
  output strb_r_r_imm_o,
  output ldrb_r_r_imm_o,
  output strh_r_r_imm_o,
  output ldrh_r_r_imm_o,
  output b_cond_o,
  output b_incond_o,
  output bl_msb_o,
  output bl_lsb_o
);

  wire comparator_28_eq, comparator_29_eq;

  Comparator #(.width(5), .mode("unsigned")) comparator_1 (
    .a(instr_i[15:11]), .b({5{1'b0}}), .eq(lsl_r_r_imm_o));  // open: gt, lt
  Comparator #(.width(5), .mode("unsigned")) comparator_2 (
    .a(instr_i[15:11]), .b(5'b00001), .eq(lsr_r_r_imm_o));  // open: gt, lt
  Comparator #(.width(5), .mode("unsigned")) comparator_3 (
    .a(instr_i[15:11]), .b(5'b00010), .eq(asr_r_r_imm_o));  // open: gt, lt
  Comparator #(.width(7), .mode("unsigned")) comparator_4 (
    .a(instr_i[15:9]), .b(7'b0001100), .eq(add_r_r_r_o));  // open: gt, lt
  Comparator #(.width(7), .mode("unsigned")) comparator_5 (
    .a(instr_i[15:9]), .b(7'b0001110), .eq(add_r_r_imm_o));  // open: gt, lt
  Comparator #(.width(7), .mode("unsigned")) comparator_6 (
    .a(instr_i[15:9]), .b(7'b0001101), .eq(sub_r_r_r_o));  // open: gt, lt
  Comparator #(.width(7), .mode("unsigned")) comparator_7 (
    .a(instr_i[15:9]), .b(7'b0001111), .eq(sub_r_r_imm_o));  // open: gt, lt
  Comparator #(.width(5), .mode("unsigned")) comparator_8 (
    .a(instr_i[15:11]), .b(5'b00100), .eq(mov_r_imm_o));  // open: gt, lt
  Comparator #(.width(5), .mode("unsigned")) comparator_9 (
    .a(instr_i[15:11]), .b(5'b00110), .eq(add_r_imm_o));  // open: gt, lt
  Comparator #(.width(5), .mode("unsigned")) comparator_10 (
    .a(instr_i[15:11]), .b(5'b00111), .eq(sub_r_imm_o));  // open: gt, lt
  Comparator #(.width(10), .mode("unsigned")) comparator_11 (
    .a(instr_i[15:6]), .b(10'h100), .eq(and_r_r_o));  // open: gt, lt
  Comparator #(.width(10), .mode("unsigned")) comparator_12 (
    .a(instr_i[15:6]), .b(10'h101), .eq(eor_r_r_o));  // open: gt, lt
  Comparator #(.width(10), .mode("unsigned")) comparator_13 (
    .a(instr_i[15:6]), .b(10'h102), .eq(lsl_r_r_o));  // open: gt, lt
  Comparator #(.width(10), .mode("unsigned")) comparator_14 (
    .a(instr_i[15:6]), .b(10'h103), .eq(lsr_r_r_o));  // open: gt, lt
  Comparator #(.width(10), .mode("unsigned")) comparator_15 (
    .a(instr_i[15:6]), .b(10'h104), .eq(asr_r_r_o));  // open: gt, lt
  Comparator #(.width(10), .mode("unsigned")) comparator_16 (
    .a(instr_i[15:6]), .b(10'h107), .eq(ror_r_r_o));  // open: gt, lt
  Comparator #(.width(10), .mode("unsigned")) comparator_17 (
    .a(instr_i[15:6]), .b(10'h109), .eq(neg_r_r_o));  // open: gt, lt
  Comparator #(.width(10), .mode("unsigned")) comparator_18 (
    .a(instr_i[15:6]), .b(10'h10c), .eq(orr_r_r_o));  // open: gt, lt
  Comparator #(.width(10), .mode("unsigned")) comparator_19 (
    .a(instr_i[15:6]), .b(10'h10f), .eq(mvn_r_r_o));  // open: gt, lt
  Comparator #(.width(7)) comparator_20 (.a(instr_i[15:9]), .b(7'b0101010), .eq(strb_r_r_r_o));  // open: gt, lt
  Comparator #(.width(7)) comparator_21 (.a(instr_i[15:9]), .b(7'b0101110), .eq(ldrb_r_r_r_o));  // open: gt, lt
  Comparator #(.width(7)) comparator_22 (.a(instr_i[15:9]), .b(7'b0101001), .eq(strh_r_r_r_o));  // open: gt, lt
  Comparator #(.width(7)) comparator_23 (.a(instr_i[15:9]), .b(7'b0101101), .eq(ldrh_r_r_r_o));  // open: gt, lt
  Comparator #(.width(5)) comparator_24 (.a(instr_i[15:11]), .b(5'b01110), .eq(strb_r_r_imm_o));  // open: gt, lt
  Comparator #(.width(5)) comparator_25 (.a(instr_i[15:11]), .b(5'b01111), .eq(ldrb_r_r_imm_o));  // open: gt, lt
  Comparator #(.width(5)) comparator_26 (.a(instr_i[15:11]), .b(5'b10000), .eq(strh_r_r_imm_o));  // open: gt, lt
  Comparator #(.width(5)) comparator_27 (.a(instr_i[15:11]), .b(5'b10001), .eq(ldrh_r_r_imm_o));  // open: gt, lt
  Comparator #(.width(4), .mode("unsigned")) comparator_28 (
    .a(instr_i[15:12]), .b(4'b1101), .eq(comparator_28_eq));  // open: gt, lt
  Comparator #(.width(4), .mode("unsigned")) comparator_29 (
    .a(instr_i[11:8]), .b(4'b1111), .eq(comparator_29_eq));  // open: gt, lt
  Comparator #(.width(5), .mode("unsigned")) comparator_30 (
    .a(instr_i[15:11]), .b(5'b11100), .eq(b_incond_o));  // open: gt, lt
  Comparator #(.width(5), .mode("unsigned")) comparator_31 (
    .a(instr_i[15:11]), .b(5'b11110), .eq(bl_msb_o));  // open: gt, lt
  Comparator #(.width(5), .mode("unsigned")) comparator_32 (
    .a(instr_i[15:11]), .b({5{1'b1}}), .eq(bl_lsb_o));  // open: gt, lt
  and AND0 (b_cond_o, comparator_28_eq, ~comparator_29_eq);  // AND_Gate

  // Other names for the same wires on the sheet: add_r_imm = add_r_imm_o; add_r_r_imm = add_r_r_imm_o;
  //   add_r_r_r = add_r_r_r_o; and_r_r = and_r_r_o; asr_r_r = asr_r_r_o; asr_r_r_imm = asr_r_r_imm_o;
  //   b_cond = b_cond_o; b_incond = b_incond_o; bl_lsb = bl_lsb_o; bl_msb = bl_msb_o; eor_r_r = eor_r_r_o;
  //   ldrb_r_r_imm = ldrb_r_r_imm_o; ldrb_r_r_r = ldrb_r_r_r_o; ldrh_r_r_imm = ldrh_r_r_imm_o;
  //   ldrh_r_r_r = ldrh_r_r_r_o; lsl_r_r = lsl_r_r_o; lsl_r_r_imm = lsl_r_r_imm_o; lsr_r_r = lsr_r_r_o;
  //   lsr_r_r_imm = lsr_r_r_imm_o; mov_r_imm = mov_r_imm_o; mvn_r_r = mvn_r_r_o; neg_r_r = neg_r_r_o;
  //   orr_r_r = orr_r_r_o; ror_r_r = ror_r_r_o; strb_r_r_imm = strb_r_r_imm_o; strb_r_r_r = strb_r_r_r_o;
  //   strh_r_r_imm = strh_r_r_imm_o; strh_r_r_r = strh_r_r_r_o; sub_r_imm = sub_r_imm_o; sub_r_r_imm = sub_r_r_imm_o;
  //   sub_r_r_r = sub_r_r_r_o

  // Notes on the sheet:
  //   Attention, votre version de Logisim
  //   ne contient pas de tracker. Si vous
  //   enregistrez votre projet, toutes les
  //   informations du tracker seront
  //   définitivement effacées.
  //   Extraction des instructions supportées
endmodule

module fetch_control_unit (
  input  [31:0] instr_i,
  output sel_cpsr_o,
  output link_en_o,
  output sel_PC_o,
  output cond_en_o
);

  wire OR0_out, OR1_out, OR2_out, OR3_out;

  or OR4 (sel_PC_o, instr_i[27], instr_i[28], instr_i[30]);
  or OR0 (OR0_out, instr_i[0], instr_i[1], instr_i[2]);
  or OR1 (OR1_out, instr_i[5], instr_i[6], instr_i[7], instr_i[8], instr_i[9]);
  or OR2 (OR2_out, instr_i[10], instr_i[11], instr_i[12], instr_i[13], instr_i[14]);
  or OR3 (OR3_out, instr_i[15], instr_i[16], instr_i[17], instr_i[18]);
  or OR5 (sel_cpsr_o, OR0_out, OR1_out, OR2_out, OR3_out);

  assign cond_en_o = instr_i[27];
  assign link_en_o = instr_i[29];

  // Other names for the same wires on the sheet: lsl_r_r_imm_s = instr_i[0]; lsr_r_r_imm_s = instr_i[1];
  //   asr_r_r_imm_s = instr_i[2]; add_r_r_r_s = instr_i[3]; add_r_r_imm_s = instr_i[4]; sub_r_r_r_s = instr_i[5];
  //   sub_r_r_imm_s = instr_i[6]; mov_r_imm_s = instr_i[7]; add_r_imm_s = instr_i[8]; sub_r_imm_s = instr_i[9];
  //   and_r_r_s = instr_i[10]; eor_r_r_s = instr_i[11]; lsl_r_r_s = instr_i[12]; lsr_r_r_s = instr_i[13];
  //   asr_r_r_s = instr_i[14]; ror_r_r_s = instr_i[15]; neg_r_r_s = instr_i[16]; orr_r_r_s = instr_i[17];
  //   mvn_r_r_s = instr_i[18]; strb_r_r_r_s = instr_i[19]; ldrb_r_r_r_s = instr_i[20]; strh_r_r_r_s = instr_i[21];
  //   ldrh_r_r_r_s = instr_i[22]; strb_r_r_imm_s = instr_i[23]; ldrb_r_r_imm_s = instr_i[24];
  //   strh_r_r_imm_s = instr_i[25]; ldrh_r_r_imm_s = instr_i[26]; b_cond_s = instr_i[27]; cond_en_s = instr_i[27];
  //   b_incond_s = instr_i[28]; bl_msb_s = instr_i[29]; link_en_s = instr_i[29]; bl_lsb_s = instr_i[30];
  //   sel_cpsr_s = sel_cpsr_o; sel_PC_s = sel_PC_o

  // Notes on the sheet:
  //   Attention, votre version de Logisim
  //   ne contient pas de tracker. Si vous
  //   enregistrez votre projet, toutes les
  //   informations du tracker seront
  //   définitivement effacées.
endmodule

module decode_control_unit (
  input  [31:0] instr_i,
  output [1:0] sel_rn_o,
  output sel_rm_o,
  output sel_rd_o
);

  wire OR1_out, OR3_out;

  or OR0 (sel_rd_o, instr_i[8], instr_i[7], instr_i[9]);
  or OR1 (OR1_out, instr_i[8], instr_i[9], instr_i[10], instr_i[11], instr_i[12]);
  or OR3 (OR3_out, instr_i[13], instr_i[14], instr_i[17], instr_i[30]);
  or OR4 (sel_rm_o, instr_i[10], instr_i[11], instr_i[12], instr_i[13], instr_i[14], instr_i[17]);
  or OR5 (sel_rn_o[1], instr_i[27], instr_i[28], instr_i[29], instr_i[30]);
  or OR2 (sel_rn_o[0], OR1_out, OR3_out);
  // Probe on sel_rn_o

  // Other names for the same wires on the sheet: lsl_r_r_imm_s = instr_i[0]; lsr_r_r_imm_s = instr_i[1];
  //   asr_r_r_imm_s = instr_i[2]; add_r_r_r_s = instr_i[3]; add_r_r_imm_s = instr_i[4]; sub_r_r_r_s = instr_i[5];
  //   sub_r_r_imm_s = instr_i[6]; mov_r_imm_s = instr_i[7]; add_r_imm_s = instr_i[8]; sub_r_imm_s = instr_i[9];
  //   and_r_r_s = instr_i[10]; eor_r_r_s = instr_i[11]; lsl_r_r_s = instr_i[12]; lsr_r_r_s = instr_i[13];
  //   asr_r_r_s = instr_i[14]; ror_r_r_s = instr_i[15]; neg_r_r_s = instr_i[16]; orr_r_r_s = instr_i[17];
  //   mvn_r_r_s = instr_i[18]; strb_r_r_r_s = instr_i[19]; ldrb_r_r_r_s = instr_i[20]; strh_r_r_r_s = instr_i[21];
  //   ldrh_r_r_r_s = instr_i[22]; strb_r_r_imm_s = instr_i[23]; ldrb_r_r_imm_s = instr_i[24];
  //   strh_r_r_imm_s = instr_i[25]; ldrh_r_r_imm_s = instr_i[26]; b_cond_s = instr_i[27]; b_incond_s = instr_i[28];
  //   bl_msb_s = instr_i[29]; bl_lsb_s = instr_i[30]; sel_rd_s = sel_rd_o; sel_rm_s = sel_rm_o;
  //   sel_rn_s[1:0] = sel_rn_o

  // Notes on the sheet:
  //   Attention, votre version de Logisim
  //   ne contient pas de tracker. Si vous
  //   enregistrez votre projet, toutes les
  //   informations du tracker seront
  //   définitivement effacées.
endmodule

module reg_bank_control_unit (
  input  [31:0] in_1,
  output out_2
);

  or OR0 (out_2, in_1[0], in_1[1], in_1[2], in_1[3], in_1[4], in_1[5], in_1[6], in_1[7], in_1[8], in_1[9], in_1[10], in_1[11], in_1[12], in_1[14], in_1[15], in_1[16], in_1[17], in_1[18], in_1[20], in_1[21], in_1[22], in_1[24], in_1[25], in_1[27], in_1[30], in_1[31]);

  // Other names for the same wires on the sheet: reg_bank_wr_s = out_2; lsl_r_r_imm_s = in_1[0]; Val_Rn[31:0] = in_1;
  //   lsr_r_r_imm_s = in_1[1]; asr_r_r_imm_s = in_1[2]; add_r_r_r_s = in_1[3]; add_r_r_imm_s = in_1[4];
  //   sub_r_r_r_s = in_1[5]; sub_r_r_imm_s = in_1[6]; mov_r_imm_s = in_1[7]; add_r_imm_s = in_1[8];
  //   sub_r_imm_s = in_1[9]; and_r_r_s = in_1[10]; eor_r_r_s = in_1[11]; lsl_r_r_s = in_1[12]; lsr_r_r_s = in_1[13];
  //   asr_r_r_s = in_1[14]; ror_r_r_s = in_1[15]; neg_r_r_s = in_1[16]; orr_r_r_s = in_1[17]; mvn_r_r_s = in_1[18];
  //   strb_r_r_r_s = in_1[19]; ldrb_r_r_r_s = in_1[20]; strh_r_r_r_s = in_1[21]; ldrh_r_r_r_s = in_1[22];
  //   strb_r_r_imm_s = in_1[23]; ldrb_r_r_imm_s = in_1[24]; strh_r_r_imm_s = in_1[25]; ldrh_r_r_imm_s = in_1[26];
  //   b_cond_s = in_1[27]; b_incond_s = in_1[28]; bl_msb_s = in_1[29]; bl_lsb_s = in_1[30]

  // Notes on the sheet:
  //   Attention, votre version de Logisim
  //   ne contient pas de tracker. Si vous
  //   enregistrez votre projet, toutes les
  //   informations du tracker seront
  //   définitivement effacées.
endmodule

module execute_control_unit (
  input  [31:0] in_1,
  output out_2,
  output [1:0] out_3,
  output [2:0] out_4,
  output [2:0] out_5,
  output [2:0] out_6,
  output out_7
);

  wire sel_mult_2_3, sel_op2_0, sel_op2_1, sel_op2_2, sel_op_alu_0, sel_op_alu_1, sel_op_shift_0,
       sel_op_shift_1, sel_op_shift_2;

  or OR7 (sel_op_alu_1, in_1[5], in_1[6], in_1[9]);
  or OR6 (sel_op_alu_0, in_1[3], in_1[4], in_1[7], in_1[8], in_1[19], in_1[20], in_1[21], in_1[22], in_1[23], in_1[24], in_1[25], in_1[26], in_1[27], in_1[28], in_1[29], in_1[30]);
  or OR0 (sel_op2_0, in_1[4], in_1[6]);
  or OR1 (sel_op2_2, in_1[7], in_1[8], in_1[9]);
  or OR3 (sel_op_shift_0, in_1[2], in_1[14]);
  or OR4 (sel_op_shift_1, in_1[0], in_1[12]);
  or OR5 (sel_op_shift_2, in_1[1], in_1[13]);
  or OR9 (out_5[1], sel_op_alu_1, in_1[11], in_1[16]);
  or OR2 (sel_op2_1, in_1[23], in_1[24], in_1[25], in_1[26], in_1[27], in_1[28], in_1[29], in_1[30]);
  or OR8 (out_5[0], sel_op_alu_0, in_1[10], in_1[18], in_1[11]);
  or OR10 (out_5[2], in_1[17], in_1[11], in_1[18]);
  Multiplexer #(.select(3), .width(2), .enable("false")) multiplexer_1 (
    .in0(2'b00), .in1(2'b01), .in2(2'b10), .in3(2'b00), .in4(2'b11), .in5(2'b00), .in6(2'b00), .in7(2'b00),
    .out(out_3), .sel({sel_op2_2, sel_op2_1, sel_op2_0}));
  // Probe on out_5
  // Probe on out_3
  Multiplexer #(.select(4), .width(3), .enable("false")) multiplexer_2 (
    .in0(3'b000), .in1(3'b001), .in2(3'b010), .in3(3'b000), .in4(3'b011), .in5(3'b000), .in6(3'b000),
    .in7(3'b000), .in8(3'b100), .in9(3'b000), .in10(3'b000), .in11(3'b000), .in12(3'b000), .in13(3'b000),
    .in14(3'b000), .in15(3'b000), .out(out_4),
    .sel({in_1[15], sel_op_shift_2, sel_op_shift_1, sel_op_shift_0}));
  // Probe on out_4
  or OR12 (out_7, in_1[12], in_1[13], in_1[14], in_1[15]);
  or OR11 (sel_mult_2_3, in_1[19], in_1[20], in_1[23], in_1[24]);
  Multiplexer #(.select(5), .width(3), .enable("false")) multiplexer_3 (
    .in0(3'b000), .in1(3'b001), .in2(3'b010), .in3(3'b000), .in4(3'b011), .in5(3'b000), .in6(3'b000),
    .in7(3'b000), .in8(3'b100), .in9(3'b000), .in10(3'b000), .in11(3'b000), .in12(3'b000), .in13(3'b000),
    .in14(3'b000), .in15(3'b000), .in16(3'b101), .in17(3'b000), .in18(3'b000), .in19(3'b000), .in20(3'b000),
    .in21(3'b000), .in22(3'b000), .in23(3'b000), .in24(3'b000), .in25(3'b000), .in26(3'b000), .in27(3'b000),
    .in28(3'b000), .in29(3'b000), .in30(3'b000), .in31(3'b000), .out(out_6),
    .sel({in_1[29], sel_mult_2_3, in_1[30], in_1[27], in_1[28]}));
  // Probe on out_6

  assign out_2 = in_1[7];

  // Other names for the same wires on the sheet: ror_r_r_s = in_1[15]; sel_op_shift_3 = in_1[15];
  //   b_incond_s = in_1[28]; sel_mult_2_0 = in_1[28]; b_cond_s = in_1[27]; sel_mult_2_1 = in_1[27];
  //   bl_lsb_s = in_1[30]; sel_mult_2_2 = in_1[30]; bl_msb_s = in_1[29]; sel_mult_2_4 = in_1[29];
  //   lsl_r_r_imm_s = in_1[0]; lsr_r_r_imm_s = in_1[1]; asr_r_r_imm_s = in_1[2]; add_r_r_r_s = in_1[3];
  //   add_r_r_imm_s = in_1[4]; sub_r_r_r_s = in_1[5]; sub_r_r_imm_s = in_1[6]; mov_r_imm_s = in_1[7];
  //   sel_operand_1_s = in_1[7]; add_r_imm_s = in_1[8]; sub_r_imm_s = in_1[9]; and_r_r_s = in_1[10];
  //   sel_op_alu_2 = in_1[10]; eor_r_r_s = in_1[11]; sel_op_alu_6 = in_1[11]; lsl_r_r_s = in_1[12];
  //   lsr_r_r_s = in_1[13]; asr_r_r_s = in_1[14]; neg_r_r_s = in_1[16]; sel_op_alu_5 = in_1[16]; orr_r_r_s = in_1[17];
  //   sel_op_alu_3 = in_1[17]; mvn_r_r_s = in_1[18]; sel_op_alu_4 = in_1[18]; strb_r_r_r_s = in_1[19];
  //   ldrb_r_r_r_s = in_1[20]; strh_r_r_r_s = in_1[21]; ldrh_r_r_r_s = in_1[22]; strb_r_r_imm_s = in_1[23];
  //   ldrb_r_r_imm_s = in_1[24]; strh_r_r_imm_s = in_1[25]; ldrh_r_r_imm_s = in_1[26]; sel_mult_2_s[2:0] = out_6;
  //   sel_op_alu_s[2:0] = out_5; sel_op_shift_s[2:0] = out_4; sel_operand_2_s[1:0] = out_3; sel_shift_s = out_7

  // Notes on the sheet:
  //   Attention, votre version de Logisim
  //   ne contient pas de tracker. Si vous
  //   enregistrez votre projet, toutes les
  //   informations du tracker seront
  //   définitivement effacées.
endmodule

module memory_access_control_unit (
  input  [31:0] in_1,
  output out_2,
  output out_3,
  output out_4,
  output out_5
);

  or OR2 (out_4, in_1[20], in_1[22], in_1[24], in_1[26]);
  or OR3 (out_5, in_1[23], in_1[24]);
  or OR0 (out_2, in_1[19], in_1[20], in_1[21], in_1[22], in_1[23], in_1[24], in_1[25], in_1[26]);
  or OR1 (out_3, in_1[19], in_1[21], in_1[23], in_1[25]);

  // Other names for the same wires on the sheet: byte_s = out_5; lsl_r_r_imm_s = in_1[0]; lsr_r_r_imm_s = in_1[1];
  //   asr_r_r_imm_s = in_1[2]; add_r_r_r_s = in_1[3]; add_r_r_imm_s = in_1[4]; sub_r_r_r_s = in_1[5];
  //   sub_r_r_imm_s = in_1[6]; mov_r_imm_s = in_1[7]; add_r_imm_s = in_1[8]; sub_r_imm_s = in_1[9];
  //   and_r_r_s = in_1[10]; eor_r_r_s = in_1[11]; lsl_r_r_s = in_1[12]; lsr_r_r_s = in_1[13]; asr_r_r_s = in_1[14];
  //   ror_r_r_s = in_1[15]; neg_r_r_s = in_1[16]; orr_r_r_s = in_1[17]; mvn_r_r_s = in_1[18]; strb_r_r_r_s = in_1[19];
  //   ldrb_r_r_r_s = in_1[20]; strh_r_r_r_s = in_1[21]; ldrh_r_r_r_s = in_1[22]; strb_r_r_imm_s = in_1[23];
  //   ldrb_r_r_imm_s = in_1[24]; strh_r_r_imm_s = in_1[25]; ldrh_r_r_imm_s = in_1[26]; b_cond_s = in_1[27];
  //   b_incond_s = in_1[28]; bl_msb_s = in_1[29]; bl_lsb_s = in_1[30]; ldr_data_s = out_4; sel_mem_s = out_2;
  //   str_data_s = out_3

  // Notes on the sheet:
  //   Attention, votre version de Logisim
  //   ne contient pas de tracker. Si vous
  //   enregistrez votre projet, toutes les
  //   informations du tracker seront
  //   définitivement effacées.
endmodule

module bus_constructor (
  input  fetch_en_i,
  input  decode_en_i,
  input  reg_bank_en_i,
  input  execute_en_i,
  input  memory_access_en_i,
  input  [3:0] cond_i,
  input  sel_cpsr_i,
  input  link_en_i,
  input  sel_PC_i,
  input  cond_en_i,
  input  [1:0] sel_rn_i,
  input  sel_rm_i,
  input  sel_rd_i,
  input  reg_bank_wr_i,
  input  sel_operand_1_i,
  input  [1:0] sel_operand_2_i,
  input  [2:0] sel_op_shift_i,
  input  [2:0] sel_op_alu_i,
  input  [2:0] sel_mult_2_i,
  input  sel_shift_i,
  input  sel_mem_i,
  input  str_data_i,
  input  ldr_data_i,
  input  byte_i,
  output [6:0] fetch_control_bus_o,
  output [5:0] decode_control_bus_o,
  output [1:0] reg_bank_control_bus_o,
  output [14:0] execute_control_bus_o,
  output [4:0] mem_control_bus_o
);


  assign decode_control_bus_o = {1'b0, sel_rd_i, link_en_i, sel_rm_i, sel_rn_i};
  assign execute_control_bus_o = {1'b0, sel_mult_2_i, sel_cpsr_i, sel_shift_i, sel_operand_1_i, sel_operand_2_i, sel_op_alu_i, sel_op_shift_i};
  assign fetch_control_bus_o = {1'b0, cond_i, cond_en_i, sel_PC_i};
  assign mem_control_bus_o = {1'b0, byte_i, ldr_data_i, str_data_i, sel_mem_i};
  assign reg_bank_control_bus_o = {reg_bank_wr_i, 1'b0};

  // Other names for the same wires on the sheet: decode_control_bus_s[4:0] = {sel_rd_i, link_en_i, sel_rm_i, sel_rn_i};
  //   sel_rn_s[1:0] = sel_rn_i; sel_rm_s = sel_rm_i; link_en_s = link_en_i; sel_rd_s = sel_rd_i;
  //   decode_en_s = decode_en_i;
  //   execute_control_bus_s[13:0] = {sel_mult_2_i, sel_cpsr_i, sel_shift_i, sel_operand_1_i, sel_operand_2_i, sel_op_alu_i, sel_op_shift_i};
  //   sel_op_shift_s[2:0] = sel_op_shift_i; sel_op_alu_s[2:0] = sel_op_alu_i; sel_operand_2_s[1:0] = sel_operand_2_i;
  //   sel_operand_1_s = sel_operand_1_i; sel_shift_s = sel_shift_i; sel_cpsr_s = sel_cpsr_i;
  //   sel_mult_2_s[2:0] = sel_mult_2_i; execute_en_s = execute_en_i;
  //   fetch_control_bus_s[5:0] = {cond_i, cond_en_i, sel_PC_i}; sel_PC_s = sel_PC_i; cond_en_s = cond_en_i;
  //   cond_s[3:0] = cond_i; fetch_en_s = fetch_en_i;
  //   mem_control_bus_s[3:0] = {byte_i, ldr_data_i, str_data_i, sel_mem_i}; sel_mem_s = sel_mem_i;
  //   str_data_s = str_data_i; ldr_data_s = ldr_data_i; byte_s = byte_i; memory_access_en_s = memory_access_en_i;
  //   reg_bank_control_bus_s[1] = reg_bank_wr_i; reg_bank_wr_s = reg_bank_wr_i; reg_bank_en_s = reg_bank_en_i

  // Notes on the sheet:
  //   Attention, votre version de Logisim
  //   ne contient pas de tracker. Si vous
  //   enregistrez votre projet, toutes les
  //   informations du tracker seront
  //   définitivement effacées.
endmodule

module bank_registers (
  input  clk_i,
  input  rst_i,
  input  [2:0] register_d_sel_i,
  input  [15:0] register_d_data_i,
  input  [2:0] register_n_sel_i,
  input  [2:0] register_m_sel_i,
  input  [2:0] register_mem_sel_i,
  input  [1:0] reg_bank_control_bus_i,
  input  [15:0] PC_fut_i,
  input  [15:0] LR_addr_i,
  input  branch_i,
  input  link_en_i,
  input  reg_bank_en_i,
  output [15:0] register_n_read_data_o,
  output [15:0] register_m_read_data_o,
  output [15:0] register_mem_read_data_o,
  output [15:0] PC_pres_o
);

  wire AND0_out, decoder_1_out0, decoder_1_out1, decoder_1_out2, decoder_1_out3, decoder_1_out4,
       decoder_1_out5, decoder_1_out6, decoder_1_out7, lr_manager_1_lr_wr_en_o, OR0_out;
  wire [15:0] lr_manager_1_lr_data_o, multiplexer_1_out, Q0, Q1, Q2, Q3, Q4, QLR, QSP;

  or OR0 (OR0_out, reg_bank_en_i, reg_bank_control_bus_i[1]);
  Decoder #(.select(3)) decoder_1 (
    .out0(decoder_1_out0), .out1(decoder_1_out1), .out2(decoder_1_out2), .out3(decoder_1_out3),
    .out4(decoder_1_out4), .out5(decoder_1_out5), .out6(decoder_1_out6), .out7(decoder_1_out7),
    .sel(register_d_sel_i), .en(OR0_out));
  LR_manager lr_manager_1 (
    .data_i(register_d_data_i), .pc_fut_lr_i(PC_fut_i), .LR_addr_i(LR_addr_i), .branch_i(branch_i),
    .write_en_i(decoder_1_out6), .link_en_i(link_en_i), .clk_i(clk_i), .rst_i(rst_i),
    .LR_data_o(lr_manager_1_lr_data_o), .LR_wr_en_o(lr_manager_1_lr_wr_en_o));
  and AND0 (AND0_out, ~link_en_i, decoder_1_out7);  // AND_Gate
  Multiplexer #(.width(16), .enable("false")) multiplexer_1 (
    .in0(PC_fut_i), .in1(register_d_data_i), .out(multiplexer_1_out), .sel(AND0_out));
  Register #(.width(16)) R0 (.D(register_d_data_i), .en(decoder_1_out0), .clk(clk_i), .Q(Q0), .clr(rst_i));
  Register #(.width(16)) R1 (.D(register_d_data_i), .en(decoder_1_out1), .clk(clk_i), .Q(Q1), .clr(rst_i));
  Register #(.width(16)) R2 (.D(register_d_data_i), .en(decoder_1_out2), .clk(clk_i), .Q(Q2), .clr(rst_i));
  Register #(.width(16)) R3 (.D(register_d_data_i), .en(decoder_1_out3), .clk(clk_i), .Q(Q3), .clr(rst_i));
  Register #(.width(16)) R4 (.D(register_d_data_i), .en(decoder_1_out4), .clk(clk_i), .Q(Q4), .clr(rst_i));
  Register #(.width(16)) SP (.D(register_d_data_i), .en(decoder_1_out5), .clk(clk_i), .Q(QSP), .clr(rst_i));
  Register #(.width(16)) LR (
    .D(lr_manager_1_lr_data_o), .en(lr_manager_1_lr_wr_en_o), .clk(clk_i), .Q(QLR), .clr(rst_i));
  Register #(.width(16)) PC (.D(multiplexer_1_out), .en(1'b1), .clk(clk_i), .Q(PC_pres_o), .clr(rst_i));
  Multiplexer #(.select(3), .width(16), .enable("false")) multiplexer_2 (
    .in0(Q0), .in1(Q1), .in2(Q2), .in3(Q3), .in4(Q4), .in5(QSP), .in6(QLR), .in7(PC_pres_o),
    .out(register_n_read_data_o), .sel(register_n_sel_i));
  Multiplexer #(.select(3), .width(16), .enable("false")) multiplexer_3 (
    .in0(Q0), .in1(Q1), .in2(Q2), .in3(Q3), .in4(Q4), .in5(QSP), .in6(QLR), .in7(PC_pres_o),
    .out(register_m_read_data_o), .sel(register_m_sel_i));
  Multiplexer #(.select(3), .width(16), .enable("false")) multiplexer_4 (
    .in0(Q0), .in1(Q1), .in2(Q2), .in3(Q3), .in4(Q4), .in5(QSP), .in6(QLR), .in7(PC_pres_o),
    .out(register_mem_read_data_o), .sel(register_mem_sel_i));

  // Other names for the same wires on the sheet: branch_s = branch_i; clk_s = clk_i; link_en_s = link_en_i;
  //   LR_addr_s[15:0] = LR_addr_i; PC_fut_s[15:0] = PC_fut_i; PC_pres[15:0] = PC_pres_o; QPC[15:0] = PC_pres_o;
  //   reg_bank_control_bus[1:0] = reg_bank_control_bus_i; reg_bank_en_s = reg_bank_en_i;
  //   reg_d_sel_s[2:0] = register_d_sel_i; reg_m_read_data_s[15:0] = register_m_read_data_o;
  //   reg_m_sel_s[2:0] = register_m_sel_i; reg_mem_read_data_s[15:0] = register_mem_read_data_o;
  //   reg_mem_sel_s[2:0] = register_mem_sel_i; reg_n_read_data_s[15:0] = register_n_read_data_o;
  //   reg_n_sel_s[2:0] = register_n_sel_i; reg_write_data_s[15:0] = register_d_data_i; rst_s = rst_i

  // Notes on the sheet:
  //   Attention, votre version de Logisim
  //   ne contient pas de tracker. Si vous
  //   enregistrez votre projet, toutes les
  //   informations du tracker seront
  //   définitivement effacées.
  //   Banque de registres
endmodule

module LR_manager (
  input  [15:0] data_i,
  input  [15:0] pc_fut_lr_i,
  input  [15:0] LR_addr_i,
  input  branch_i,
  input  write_en_i,
  input  link_en_i,
  input  clk_i,
  input  rst_i,
  output [15:0] LR_data_o,
  output LR_wr_en_o
);

  wire AND1_out, link_en_d1_s, OR0_out;
  wire [15:0] multiplexer_1_out;

  Multiplexer #(.width(16), .enable("false")) multiplexer_1 (
    .in0(data_i), .in1(pc_fut_lr_i), .out(multiplexer_1_out), .sel(AND1_out));
  and AND1 (AND1_out, branch_i, link_en_i);
  D_Flip_Flop d_ff_1 (.D(link_en_i), .clk(clk_i), .Q(link_en_d1_s), .reset(rst_i));  // open: Qn, preset
  or OR0 (OR0_out, write_en_i, link_en_i);
  Multiplexer #(.width(16), .enable("false")) multiplexer_2 (
    .in0(multiplexer_1_out), .in1(LR_addr_i), .out(LR_data_o), .sel(link_en_d1_s));
  or OR1 (LR_wr_en_o, OR0_out, link_en_d1_s);

  // Other names for the same wires on the sheet: clk_s = clk_i; link_en_s = link_en_i; rst_s = rst_i

  // Notes on the sheet:
  //   Attention, votre version de Logisim
  //   ne contient pas de tracker. Si vous
  //   enregistrez votre projet, toutes les
  //   informations du tracker seront
  //   définitivement effacées.
endmodule

module execute (
  input  [15:0] reg_data_n_i,
  input  [15:0] reg_data_m_i,
  input  [2:0] imm3,
  input  [4:0] imm5,
  input  [10:0] offset_incond,
  input  [7:0] offset_cond,
  input  [7:0] imm8,
  input  [14:0] execute_control_bus,
  input  rst_i,
  input  clk_i,
  input  execute_en_i,
  output [15:0] data_out_o,
  output [3:0] cpsr_o
);

  wire bloc_alu_carry_o, bloc_alu_overflow_o;
  wire [3:0] bloc_zcnv_unit_z_o, sel_shift_data_s;
  wire [15:0] bloc_shift_shift_data_out_o, mult_2_out_s, operand_1_s, operand_2_s;

  shift bloc_shift (
    .operand_i(operand_1_s), .sel_shift_data_i(sel_shift_data_s), .sel_op_shift_i(execute_control_bus[2:0]),
    .shift_data_out_o(bloc_shift_shift_data_out_o));
  Multiplexer #(.select(2), .width(16), .enable("false")) multiplexer_1 (
    .in0(reg_data_m_i), .in1({{14{imm3[2]}}, imm3[1:0]}), .in2(mult_2_out_s),
    .in3({{9{imm8[7]}}, imm8[6:0]}), .out(operand_2_s), .sel(execute_control_bus[7:6]));
  Multiplexer #(.width(16), .enable("false")) multiplexer_2 (
    .in0(reg_data_n_i), .in1({16{1'b0}}), .out(operand_1_s), .sel(execute_control_bus[8]));
  Multiplexer #(.width(4), .enable("false")) multiplexer_3 (
    .in0(imm5[3:0]), .in1(reg_data_m_i[3:0]), .out(sel_shift_data_s), .sel(execute_control_bus[9]));
  mult_2 bloc_mult_2 (
    .imm5_i(imm5), .offset_incond_i(offset_incond), .offset_cond_i(offset_cond),
    .sel_mult_2_i(execute_control_bus[13:11]), .mult_2_out(mult_2_out_s));
  alu bloc_alu (
    .operand_1_i(bloc_shift_shift_data_out_o), .operand_2_i(operand_2_s),
    .sel_op_alu_i(execute_control_bus[5:3]), .alu_data_out_o(data_out_o), .carry_o(bloc_alu_carry_o),
    .overflow_o(bloc_alu_overflow_o));
  zcnv_unit bloc_zcnv_unit (
    .data_i(data_out_o), .carry_i(bloc_alu_carry_o), .overflow_i(bloc_alu_overflow_o),
    .z_o(bloc_zcnv_unit_z_o[0]), .c_o(bloc_zcnv_unit_z_o[1]), .n_o(bloc_zcnv_unit_z_o[2]),
    .v_o(bloc_zcnv_unit_z_o[3]));
  Register #(.width(4)) register_1 (
    .D(bloc_zcnv_unit_z_o), .en(execute_control_bus[10]), .clk(clk_i), .Q(cpsr_o), .clr(rst_i));

  // Other names for the same wires on the sheet: imm3_s[2:0] = imm3; imm8_s[7:0] = imm8; clk_s = clk_i;
  //   cpsr_s[3:0] = cpsr_o; data_out_s[15:0] = data_out_o; execute_control_bus_s[14:0] = execute_control_bus;
  //   sel_op_shift[2:0] = execute_control_bus[2:0]; sel_op_alu[2:0] = execute_control_bus[5:3];
  //   sel_operand_2_s[1:0] = execute_control_bus[7:6]; sel_operand_1_s = execute_control_bus[8];
  //   sel_shift_i = execute_control_bus[9]; flag_CPSR = execute_control_bus[10];
  //   sel_mult_2_s[2:0] = execute_control_bus[13:11]; execute_en_s = execute_en_i; imm5_s[4:0] = imm5;
  //   offset_cond_s[7:0] = offset_cond; offset_incond_s[10:0] = offset_incond; reg_data_m_s[15:0] = reg_data_m_i;
  //   reg_data_n_s[15:0] = reg_data_n_i; rst_s = rst_i

  // Notes on the sheet:
  //   Attention, votre version de Logisim
  //   ne contient pas de tracker. Si vous
  //   enregistrez votre projet, toutes les
  //   informations du tracker seront
  //   définitivement effacées.
  //   Entité EXECUTE
endmodule

module mult_2 (
  input  [4:0] imm5_i,
  input  [10:0] offset_incond_i,
  input  [7:0] offset_cond_i,
  input  [2:0] sel_mult_2_i,
  output [15:0] mult_2_out
);

  wire [0:0] offset_cond_ext_signed_incr_x2_s;
  wire [15:0] imm5_ext_unsigned_s, imm5_ext_x2_s, offset_cond_ext_signed_incr_s, offset_cond_ext_signed_s,
       offset_incond_ext_signed_incr_s, offset_incond_ext_signed_incr_x2_s, offset_incond_ext_signed_s,
       offset_incond_ext_signed_shifted_incr_s, offset_incond_ext_signed_shifted_s,
       offset_incond_ext_unsigned_incr_s, offset_incond_ext_unsigned_incr_x2_s, offset_incond_ext_unsigned_s;
  wire [15:1] offset_cond_ext_signed_incr_aligned_s;

  assign imm5_ext_unsigned_s = {{11{1'b0}}, imm5_i};  // Bit_Extender bit_extender_1
  assign offset_incond_ext_signed_s = {{5{offset_incond_i[10]}}, offset_incond_i};  // Bit_Extender bit_extender_2
  assign offset_incond_ext_unsigned_s = {{5{1'b0}}, offset_incond_i};  // Bit_Extender bit_extender_3
  assign offset_cond_ext_signed_s = {{8{offset_cond_i[7]}}, offset_cond_i};  // Bit_Extender bit_extender_4
  Adder #(.width(16)) adder_1 (
    .a(offset_incond_ext_signed_s), .b(16'h2), .out(offset_incond_ext_signed_incr_s));  // open: cin, cout
  Adder #(.width(16)) adder_2 (
    .a(offset_cond_ext_signed_s), .b(16'h2), .out(offset_cond_ext_signed_incr_s));  // open: cin, cout
  Adder #(.width(16)) adder_3 (
    .a(offset_incond_ext_signed_shifted_s), .b(16'h2), .out(offset_incond_ext_signed_shifted_incr_s));  // open: cin, cout
  Adder #(.width(16)) adder_4 (
    .a(offset_incond_ext_unsigned_s), .b(16'h2), .out(offset_incond_ext_unsigned_incr_s));  // open: cin, cout
  Shifter #(.width(16)) shifter_1 (.in(imm5_ext_unsigned_s), .\dist (4'b0001), .out(imm5_ext_x2_s));
  Shifter #(.width(16)) shifter_2 (
    .in(offset_incond_ext_signed_incr_s), .\dist (4'b0001), .out(offset_incond_ext_signed_incr_x2_s));
  Shifter #(.width(16)) shifter_3 (
    .in(offset_cond_ext_signed_incr_s), .\dist (4'b0001),
    .out({offset_cond_ext_signed_incr_aligned_s, offset_cond_ext_signed_incr_x2_s[0]}));
  Shifter #(.width(16)) shifter_4 (
    .in(offset_incond_ext_unsigned_incr_s), .\dist (4'b0001), .out(offset_incond_ext_unsigned_incr_x2_s));
  Shifter #(.width(16)) shifter_5 (
    .in(offset_incond_ext_signed_s), .\dist (4'b1100), .out(offset_incond_ext_signed_shifted_s));
  Multiplexer #(.select(3), .width(16), .enable("false")) multiplexer_1 (
    .in0(imm5_ext_x2_s), .in1(offset_incond_ext_signed_incr_x2_s),
    .in2({offset_cond_ext_signed_incr_aligned_s, 1'b0}), .in3(offset_incond_ext_unsigned_incr_x2_s),
    .in4(imm5_ext_unsigned_s), .in5(offset_incond_ext_signed_shifted_s), .in6(offset_incond_ext_unsigned_s),
    .in7({16{1'b0}}), .out(mult_2_out), .sel(sel_mult_2_i));

  // Other names for the same wires on the sheet: imm5_s[4:0] = imm5_i; mult_2_out_s[15:0] = mult_2_out;
  //   offset_cond_ext_signed_incr_x2_s[15:1] = offset_cond_ext_signed_incr_aligned_s;
  //   offset_cond_s[7:0] = offset_cond_i; offset_incond_s[10:0] = offset_incond_i; sel_mult_2_s[2:0] = sel_mult_2_i

  // Notes on the sheet:
  //   Attention, votre version de Logisim
  //   ne contient pas de tracker. Si vous
  //   enregistrez votre projet, toutes les
  //   informations du tracker seront
  //   définitivement effacées.
  //   Extensions nécessaires
  //   Incréments
  //   x2 => shift à gauche = pas de logique
  //   Utilisé pour le BL MSB
  //   Utilisé pour le BL LSB (or logique)
endmodule

module shift (
  input  [15:0] operand_i,
  input  [3:0] sel_shift_data_i,
  input  [2:0] sel_op_shift_i,
  output [15:0] shift_data_out_o
);

  wire [15:0] shif_arithm, shif_log_left, shif_log_right, shif_rot_right;

  Shifter #(.width(16), .shift("ar")) shifter_1 (.in(operand_i), .\dist (sel_shift_data_i), .out(shif_arithm));
  Shifter #(.width(16)) shifter_2 (.in(operand_i), .\dist (sel_shift_data_i), .out(shif_log_left));
  Shifter #(.width(16), .shift("lr")) shifter_3 (.in(operand_i), .\dist (sel_shift_data_i), .out(shif_log_right));
  Shifter #(.width(16), .shift("rr")) shifter_4 (.in(operand_i), .\dist (sel_shift_data_i), .out(shif_rot_right));
  Multiplexer #(.select(3), .width(16), .enable("false")) multiplexer_1 (
    .in0(operand_i), .in1(shif_arithm), .in2(shif_log_left), .in3(shif_log_right), .in4(shif_rot_right),
    .in5({16{1'b0}}), .in6({16{1'b0}}), .in7({16{1'b0}}), .out(shift_data_out_o), .sel(sel_op_shift_i));

  // Other names for the same wires on the sheet: operand_s[15:0] = operand_i; sel_op_shift_s[2:0] = sel_op_shift_i;
  //   sel_shift_data_s[3:0] = sel_shift_data_i

  // Notes on the sheet:
  //   Attention, votre version de Logisim
  //   ne contient pas de tracker. Si vous
  //   enregistrez votre projet, toutes les
  //   informations du tracker seront
  //   définitivement effacées.
endmodule

module alu (
  input  [15:0] operand_1_i,
  input  [15:0] operand_2_i,
  input  [2:0] sel_op_alu_i,
  output [15:0] alu_data_out_o,
  output carry_o,
  output overflow_o
);

  wire carry_add, carry_sub, comparator_1_eq, comparator_2_eq, not_3_out, not_4_out;
  wire [15:0] add, adder_3_out, and_1, compl_2, inv_1, not_2_out, or_1, sub, xor_1;

  Adder #(.width(16)) adder_1 (.a(inv_1), .b(16'h1), .out(compl_2));  // open: cin, cout
  Adder #(.width(16)) adder_2 (.a(operand_1_i), .b(operand_2_i), .out(add), .cout(carry_add));  // open: cin
  Subtractor #(.width(16)) subtractor_1 (.a(operand_1_i), .b(operand_2_i), .out(sub), .bout(carry_sub));  // open: bin
  assign and_1 = operand_1_i & operand_2_i;  // AND_Gate AND0, 16 bits wide
  assign or_1 = operand_1_i | operand_2_i;  // OR_Gate OR0, 16 bits wide
  assign inv_1 = ~operand_1_i;  // NOT_Gate not_1, 16 bits wide
  assign xor_1 = operand_1_i ^ operand_2_i;  // XOR_Gate XOR0, 16 bits wide
  Multiplexer #(.select(3), .width(16), .enable("false")) multiplexer_1 (
    .in0(operand_1_i), .in1(add), .in2(sub), .in3(and_1), .in4(or_1), .in5(inv_1), .in6(compl_2),
    .in7(xor_1), .out(alu_data_out_o), .sel(sel_op_alu_i));
  assign not_2_out = ~operand_2_i;  // NOT_Gate not_2, 16 bits wide
  Multiplexer #(.enable("false")) multiplexer_2 (
    .in0(carry_add), .in1(carry_sub), .out(carry_o), .sel(sel_op_alu_i[1]));
  Adder #(.width(16)) adder_3 (.a(not_2_out), .b(16'h1), .out(adder_3_out));  // open: cin, cout
  Comparator #(.width(2)) comparator_1 (
    .a({2{add[15]}}), .b({operand_2_i[15], operand_1_i[15]}), .eq(comparator_1_eq));  // open: gt, lt
  Comparator #(.width(2)) comparator_2 (
    .a({2{sub[15]}}), .b({adder_3_out[15], operand_1_i[15]}), .eq(comparator_2_eq));  // open: gt, lt
  not not_3 (not_3_out, comparator_1_eq);
  not not_4 (not_4_out, comparator_2_eq);
  Multiplexer #(.select(3), .enable("false")) multiplexer_3 (
    .in0(1'b0), .in1(not_3_out), .in2(not_4_out), .in3(1'b0), .in4(1'b0), .in5(1'b0), .in6(1'b0), .in7(1'b0),
    .out(overflow_o), .sel(sel_op_alu_i));

  // Other names for the same wires on the sheet: operand_2_s[15:0] = operand_2_i; operand_1_s[15:0] = operand_1_i;
  //   carry_s = carry_o; data_out_s[15:0] = alu_data_out_o; overflow_s = overflow_o; sel_op_alu_s[2:0] = sel_op_alu_i

  // Notes on the sheet:
  //   Attention, votre version de Logisim
  //   ne contient pas de tracker. Si vous
  //   enregistrez votre projet, toutes les
  //   informations du tracker seront
  //   définitivement effacées.
endmodule

module zcnv_unit (
  input  [15:0] data_i,
  input  carry_i,
  input  overflow_i,
  output z_o,
  output c_o,
  output n_o,
  output v_o
);

  Comparator #(.width(16)) comparator_1 (.a(data_i), .b({16{1'b0}}), .eq(z_o));  // open: gt, lt

  assign c_o = carry_i;
  assign n_o = data_i[15];
  assign v_o = overflow_i;

  // Other names for the same wires on the sheet: carry_s = carry_i; data_s[15:0] = data_i; overflow_s = overflow_i

  // Notes on the sheet:
  //   Attention, votre version de Logisim
  //   ne contient pas de tracker. Si vous
  //   enregistrez votre projet, toutes les
  //   informations du tracker seront
  //   définitivement effacées.
endmodule

module memory_access (
  input  [15:0] mem_data_i,
  input  [15:0] reg_data_i,
  input  [15:0] data_i,
  input  [4:0] memory_control_bus_i,
  input  rst_i,
  input  clk_i,
  input  mem_access_en_i,
  output [14:0] mem_data_adr_o,
  output [15:0] mem_adr_byte_o,
  output [15:0] mem_data_out_o,
  output [15:0] mem_out_o,
  output str_data_o,
  output ldr_data_o,
  output high_byte_o,
  output low_byte_o
);

  wire AND0_out, AND1_out, not_1_out, not_2_out, OR0_out;
  wire [15:0] register_1_q;

  or OR0 (OR0_out, memory_control_bus_i[1], memory_control_bus_i[2]);
  Multiplexer #(.width(16), .enable("false")) multiplexer_1 (
    .in0(register_1_q), .in1(data_i), .out(mem_adr_byte_o), .sel(OR0_out));
  Register #(.width(16)) register_1 (.D(mem_adr_byte_o), .en(1'b1), .clk(clk_i), .Q(register_1_q), .clr(rst_i));
  not not_1 (not_1_out, mem_adr_byte_o[0]);
  not not_2 (not_2_out, memory_control_bus_i[3]);
  and AND0 (AND0_out, memory_control_bus_i[3], mem_adr_byte_o[0]);
  and AND1 (AND1_out, memory_control_bus_i[3], not_1_out);
  Multiplexer #(.width(16), .enable("false")) multiplexer_2 (
    .in0(data_i), .in1(mem_data_i), .out(mem_out_o), .sel(memory_control_bus_i[0]));
  or OR1 (high_byte_o, not_2_out, AND0_out);
  or OR2 (low_byte_o, not_2_out, AND1_out);

  assign ldr_data_o = memory_control_bus_i[2];
  assign mem_data_adr_o = mem_adr_byte_o[15:1];
  assign mem_data_out_o = reg_data_i;
  assign str_data_o = memory_control_bus_i[1];

  // Other names for the same wires on the sheet: data_s[15:0] = data_i; high_byte_s = high_byte_o;
  //   low_byte_s = low_byte_o; mem_access_en_s = mem_access_en_i; adresse_offset_s = mem_adr_byte_o[0];
  //   mem_adr_byte_s[15:0] = mem_adr_byte_o; mem_data_adr_s[14:0] = mem_adr_byte_o[15:1];
  //   mem_data_s[15:0] = mem_data_i; mem_out_s[15:0] = mem_out_o; memory_control_bus_s[4:0] = memory_control_bus_i;
  //   sel_mem_s = memory_control_bus_i[0]; str_data_s = memory_control_bus_i[1]; ldr_data_s = memory_control_bus_i[2];
  //   byte_s = memory_control_bus_i[3]; mem_data_out_s[15:0] = reg_data_i; reg_data_s[15:0] = reg_data_i

  // Notes on the sheet:
  //   Attention, votre version de Logisim
  //   ne contient pas de tracker. Si vous
  //   enregistrez votre projet, toutes les
  //   informations du tracker seront
  //   définitivement effacées.
  //   Entité MEMORY ACCESS
endmodule
